// Logisim project ALU.circ as structural Verilog: 1 circuit, main circuit main
module main (
  input  cs0,
  input  cs1,
  input  cs2,
  input  A0,
  input  A1,
  input  A2,
  input  A3,
  input  B0,
  input  B1,
  input  B2,
  input  B3,
  output s0,
  output s1,
  output Z,
  output Ci,
  output Xi0,
  output Xi1,
  output Xi2,
  output Xi3,
  output C,
  output f0,
  output Yi0,
  output f1,
  output Yi1,
  output f2,
  output Yi2,
  output f3,
  output Yi3,
  output S
);

  wire n7404_1_p2, n7404_1_p4, n7404_1_p6, n7404_1_p9, n7408_1_p3, n7408_1_p6, n7408_1_p11, n7408_1_p14,
       n7408_2_p6, n7408_2_p11, n7408_3_p3, n7408_3_p6, n7408_3_p11, n7408_3_p14, n7432_1_p6, n7432_1_p10,
       n7486_1_p3, n7486_1_p6, n7486_1_p11, n7486_1_p14, n7486_2_p3, n7486_2_p6, n7486_2_p11, n7486_2_p14;

  // _7404 7404_1: pin names not known; wires that end beside it: cs0, n7404_1_p2, cs1, n7404_1_p4, cs2, n7404_1_p6, 1'b0, 1'b1, n7404_1_p9, Z
  // _7408 7408_1: pin names not known; wires that end beside it: cs1, B0, n7408_1_p3, cs1, B1, n7408_1_p6, 1'b0, 1'b1, B3, cs1, n7408_1_p11, B2, cs1, n7408_1_p14
  // _7408 7408_2: pin names not known; wires that end beside it: n7404_1_p2, n7404_1_p4, s0, cs1, cs2, n7408_2_p6, 1'b0, 1'b1, n7404_1_p2, n7408_2_p6, n7408_2_p11, n7404_1_p6, cs1, Ci
  // _7408 7408_3: pin names not known; wires that end beside it: A0, B0, n7408_3_p3, A1, B1, n7408_3_p6, 1'b0, 1'b1, A3, B3, n7408_3_p11, A2, B2, n7408_3_p14
  // _7486 7486_1: pin names not known; wires that end beside it: cs0, n7408_1_p3, n7486_1_p3, cs0, n7408_1_p6, n7486_1_p6, 1'b0, 1'b1, n7408_1_p11, cs0, n7486_1_p11, n7408_1_p14, cs0, n7486_1_p14
  // _7486 7486_2: pin names not known; wires that end beside it: A0, n7408_2_p11, n7486_2_p3, A1, n7408_2_p11, n7486_2_p6, 1'b0, 1'b1, A3, n7408_2_p11, n7486_2_p11, A2, n7408_2_p11, n7486_2_p14
  // _74157 74157_1: pin names not known; wires that end beside it: s1, n7486_1_p3, 1'b0, Yi0, n7486_1_p6, 1'b0, Yi1, 1'b0, 1'b1, 1'b0, n7486_1_p11, 1'b0, Yi3, n7486_1_p14, 1'b0, Yi2
  // _74157 74157_2: pin names not known; wires that end beside it: s0, n7486_2_p3, n7408_3_p3, Xi0, n7486_2_p6, n7408_3_p6, Xi1, 1'b0, 1'b1, 1'b0, n7486_2_p11, n7408_3_p11, Xi3, n7486_2_p14, n7408_3_p14, Xi2
  // _7432 7432_1: pin names not known; wires that end beside it: s0, n7408_2_p6, s1, f0, f1, n7432_1_p6, 1'b0, 1'b1, Yi3, n7432_1_p10, n7404_1_p9, f2, n7432_1_p6, n7432_1_p10, n7404_1_p9
  // _7483 7483_1: pin names not known; wires that end beside it: Xi3, f2, Xi2, Yi2, 1'b1, f1, Yi1, Xi1, Yi3, f3, C, Ci, 1'b0, Yi0, Xi0, f0

  assign S = f3;

  // Notes on the sheet:
  //   cs1.cs2
  //   cs2.cs1.cs0"
  //   My1
  //   Mx00
  //   Mx01
  //   Mx02
  //   Mx03
  //   Mx
endmodule
